# Fritzing sketch RabbitHutchDoor (saved by Fritzing 0.9.4)
circuit board: 5.53614cm x 4.23368cm
breadboards: 1

parts:
  Servo = male pin header, 3 pins [form="♂ (male)"]
  5V = screw terminal, 2 pins
  Buttons = male pin header, 6 pins [form="♂ (male)"]
  IRL_520N = Basic FET N-Channel [package="TO220 [THT]"]
  DHT_22 = Humidity and Temperature Sensor RHT03
  10k = Resistor [tolerance=±5% resistance=10k package=THT]
  WeMos_D1_Mini1 = WeMos D1 Mini
  470 = Resistor [tolerance=±5% resistance=470 package=THT]
  470k = Resistor [tolerance=±5% resistance=470k package=THT]

nets:
  N1: Servo.pin1, WeMos_D1_Mini1.D2
  N2: Servo.pin2, 5V.pin1, WeMos_D1_Mini1.5V, 470k.Pin_0
  N3: Servo.pin3, IRL_520N.drain, DHT_22.GND_1, DHT_22.GND_2
  N4: 5V.pin2, Buttons.pin1, Buttons.pin3, Buttons.pin5, IRL_520N.source, WeMos_D1_Mini1.G
  N5: Buttons.pin2, WeMos_D1_Mini1.D6
  N6: Buttons.pin4, WeMos_D1_Mini1.D1
  N7: Buttons.pin6, WeMos_D1_Mini1.RST, 470.Pin_0
  N8: IRL_520N.gate, WeMos_D1_Mini1.D5
  VCC: DHT_22.Vcc, 10k.Pin_1, WeMos_D1_Mini1.3V3
  N9: DHT_22.Data-signal, 10k.Pin_0, WeMos_D1_Mini1.D7
  N10: WeMos_D1_Mini1.A0, 470k.Pin_1
  N11: WeMos_D1_Mini1.D0, 470.Pin_1

notes:
  5V
  GND
  open
  close
  reset
