# Fritzing sketch BatteryLight (saved by Fritzing 1.0.1rc)
circuit board: 9.3cm x 5.3cm
breadboards: 1

parts:
  Bat = prefix0000 [form="♂ (male)"]
  IRL_540N = Basic FET N-Channel [package="TO220 [THT]"]
  R1 = Resistor [tolerance=±5% power=0.25 resistance=1M package=THT]
  Out- = male pin header, 1 pin [form="♂ (male)"]
  Out+ = male pin header, 1 pin [form="♂ (male)"]
  In+ = male pin header, 1 pin [form="♂ (male)"]
  In- = male pin header, 1 pin [form="♂ (male)"]
  In+_2 = male pin header, 1 pin [form="♂ (male)"]
  LED_In- = male pin header, 1 pin [form="♂ (male)"]
  Out+_2 = male pin header, 1 pin [form="♂ (male)"]
  Out-_2 = male pin header, 1 pin [form="♂ (male)"]
  PWM+ = male pin header, 1 pin [form="♂ (male)"]
  PWM- = male pin header, 1 pin [form="♂ (male)"]
  MCP1700 = Voltage Regulator [package=to-92]
  1uF = Ceramic Capacitor [capacitance=1µF voltage=35V package="200 mil [THT, multilayer]"]
  1uF_2 = Ceramic Capacitor [capacitance=1µF voltage=35V package="200 mil [THT, multilayer]"]
  NRF24LO1 = NRF24L01+ Breakout Board
  100k = Resistor [tolerance=±5% power=0.25 resistance=100k package=THT]
  R4 = Resistor [tolerance=±5% power=0.25 resistance=470k package=THT]
  AM312 = male pin header, 3 pins [form="♂ (male)"]
  BH1750 = male pin header, 4 pins [form="♂ (male)"]
  LED = prefix0000 [form="♂ (male)"]
  Attiny84 = IC, DIP package, 14 pins [chip_label=ATtiny84]

nets:
  N1: Bat.connector0, R1.Pin_0, In+.pin1, MCP1700.IN, 1uF_2.1, R4.Pin_0, Attiny84.pin1
  GND: Bat.connector1, IRL_540N.source, MCP1700.GND, 1uF.0, 1uF_2.0, NRF24LO1.GND, 100k.Pin_1, AM312.pin2, BH1750.pin2, Attiny84.pin14
  N2: IRL_540N.gate, Attiny84.pin10
  N3: IRL_540N.drain, R1.Pin_1, Out-.pin1, In-.pin1, LED_In-.pin1, PWM-.pin1
  N4: Out+.pin1, In+_2.pin1
  N5: Out+_2.pin1, LED.connector0
  N6: Out-_2.pin1, LED.connector1
  N7: PWM+.pin1, Attiny84.pin6
  N8: MCP1700.OUT, 1uF.1, NRF24LO1.VCC, AM312.pin1, BH1750.pin1
  N9: NRF24LO1.CE, Attiny84.pin3
  N10: NRF24LO1.CS, Attiny84.pin5
  N11: NRF24LO1.SCK, Attiny84.pin9
  N12: NRF24LO1.MOSI, Attiny84.pin8
  N13: NRF24LO1.MISO, Attiny84.pin7
  N14: 100k.Pin_0, R4.Pin_1, Attiny84.pin13
  N15: AM312.pin3, Attiny84.pin2
  N16: BH1750.pin3, Attiny84.pin12
  N17: BH1750.pin4, Attiny84.pin11

notes:
  VCC
  MT3608
  LED source
  Battery Light V1.0
  +
  Battery Light, 1.0
